# Fritzing sketch garage_remote_sketch (saved by Fritzing 0.9.3b)
circuit board: 5.7799cm x 4.55476cm
breadboards: 1

parts:
  WeMos_D1_Mini1 = WeMos D1 Mini
  LED_5V = LED - 5mm [color="Green (570nm)" package="5 mm [THT]"]
  R1 = Resistor [tolerance=±5% resistance=1.5k package=THT]
  S1 = Pushbutton [package="[THT]"]
  PNP = pnp-Powertransistor [package="TO220 [THT]"]
  U1 = Voltage Regulator - 5V [package="TO220 [THT]"]

nets:
  N1: WeMos_D1_Mini1.5V, LED_5V.anode, U1.output_voltage
  N2: WeMos_D1_Mini1.D5, S1.Pin_1, S1.Pin_2
  N3: WeMos_D1_Mini1.D6, R1.Pin_1
  GND: WeMos_D1_Mini1.G, S1.Pin_3, S1.Pin_4, PNP.collector, U1.GND
  N4: LED_5V.cathode, PNP.emitter
  N5: R1.Pin_0, PNP.base
  12V: U1.input_voltage
